# Fritzing sketch pdb (saved by Fritzing 0.9.3b)

parts:
  U1 = NodeMCU V1.0
  IC1 = MCP3008 8-channel 10-bit ADC [part_number=MCP3008]
  U2 = LM2596 step down module
  U4 = LM2596 step down module
  C1 = Electrolytic Capacitor [capacitance=1µF package="100 mil [THT, electrolytic]"]
  R1 = Photocell (LDR) [package=THT]
  R2 = Resistor [tolerance=±5% resistance=220 package=THT]
  부품3 = FC-28 Soil Hygrometer Module
  부품4 = FC-28 Soil Hygrometer Module - Probe
  U5 = LM2596 step down module
  J1 = Basic Servo
  U6 = 2-Channel 5v Relay Shield [package=relay-2ch5v10a]
  J2 = Power Jack [package=power_jack_pth_lock]
  M1 = DC Motor
  F1 = Fan - Ventilador [package=THT]
  F2 = Fan - Ventilador [package=THT]
  F3 = Fan - Ventilador [package=THT]
  J3 = Power Jack [package=power_jack_pth_lock]
  J4 = Power Jack [package=power_jack_pth_lock]
  J5 = Power Jack [package=power_jack_pth_lock]

nets:
  N1: U1.D1, U6.IN1
  N2: U1.D2, U6.IN2
  GND: U1.GND, IC1.no_name_yet#14, U2.IN+, U2.IN-, U2.OUT-, J1.gnd, U6.GND, J4.PWR
  N3: U1.D5, IC1.no_name_yet#13
  N4: U1.D6, IC1.no_name_yet#12
  N5: U1.D7, IC1.no_name_yet#11
  N6: U1.D8, IC1.no_name_yet#10
  VCC: U1.Vin, U2.OUT+, J1.vcc, U6.VCC
  N7: IC1.no_name_yet#1, 부품3.DO
  N8: IC1.no_name_yet#2, R1.pin_1, R2.Pin_0
  N9: IC1.no_name_yet#9, U4.IN+, U4.IN-, U4.OUT-, R2.Pin_1, 부품3.GND, J5.PWR
  N10: IC1.no_name_yet#16, U4.OUT+, C1.-, R1.pin_0, 부품3.VCC
  N11: 부품3.POS, 부품4.POS
  N12: 부품3.NEG, 부품4.NEG
  N13: U5.IN+, U5.IN-, U5.OUT-, J2.GND, J2.PWR, M1.pin_2
  N14: U5.OUT+, U6.K2-In
  5V: U6.K1-In, F1.5V, F2.5V, F3.5V, J3.PWR
  GND_2: U6.K1-On, F1.GND, F2.GND, F3.GND
  N15: U6.K2-Off, M1.pin_1

custom parts:
  NodeMCU V1.0: ESP8266 based NodeMCU
  LM2596 step down module: LM2596 DC-DC step down power supply module 3 A.
  FC-28 Soil Hygrometer Module: The FC-28 is a soil hygrometer module that uses the Texas Instruments LM393 comparator chip to provide an analog measurement of soil humidity. The digital output is high when soil moisture is over a certain threshold, as determined by adjusting the potentiometer.
  FC-28 Soil Hygrometer Module - Probe: The FC-28 is a soil hygrometer module that uses the Texas Instruments LM393 comparator chip to provide an analog measurement of soil humidity.
  2-Channel 5v Relay Shield: 2 Channel 5v Relay Shield w. 2x SPD-06VDC-SD-C
  Fan - Ventilador: Ventilador de 2 pines, se encuentra comunmente en computadoras de escritorio
